# Fritzing sketch FlightController (saved by Fritzing 1.0.5)
perfboards: 1

parts:
  Teensy1 = Teensy 3.6 (Basic)
  R2 = Resistor [tolerance=±5% resistance=100 package="2512 [SMD]"]
  LED1 = smd LED [color="Red (633nm)" package="0603 [SMD]"]
  LED2 = smd LED [color="Green (555nm)" package="0603 [SMD]"]
  J1 = Piezo Speaker
  JP1 = Header 4 [package=1x04-smd]
  Part1 = InvenSense MPU6050
  JP2 = Header 3 [package=1x03-1mm-ra]
  JP3 = M16 [package=1x16_machine-pin-header_lock.004]
  JP4 = M16 [package=1x16_machine-pin-header_lock.004]
  R4 = Resistor [tolerance=±5% resistance=3.3k package="0402 [SMD]"]
  R5 = Resistor [tolerance=±5% resistance=3.3k package="0402 [SMD]"]
  JP5 = Header 2 [package=jst-2-smd]

nets:
  GND: Teensy1.GND, Teensy1.GND1, JP3.1
  N1: Teensy1.D0, Part1.INT
  N2: Teensy1.D3, JP1.1
  N3: Teensy1.D4, JP1.2
  N4: Teensy1.D5, JP1.3
  N5: Teensy1.D6, JP1.4
  N6: Teensy1.D9, JP2.3
  N7: Teensy1.A4/D18, Part1.SDA
  N8: Teensy1.A5/D19, Part1.SCL
  N9: Teensy1.3V3, Teensy1.3V3_1
  N10: Teensy1.Vin, JP4.1
  N11: Teensy1.D27, R2.Pin_0
  N12: Teensy1.D28, R4.Pin_0
  N13: Teensy1.D30, R5.Pin_0
  N14: R2.Pin_1, J1.pin2
  N15: LED1.cathode, JP3.12
  N16: LED1.anode, R4.Pin_1
  N17: LED2.cathode, JP3.14
  N18: LED2.anode, R5.Pin_1
  N19: J1.pin1, JP3.16
  N20: Part1.VCC, JP4.2
  N21: Part1.GND, JP3.2
  N22: JP2.1, JP4.16
  N23: JP2.2, JP3.15
  N24: JP3.3, JP5.2
  N25: JP4.3, JP5.1

notes:
  Motor ESC Pins:
  Front Left: 3
  Front Rigth: 5
  Rear Left: 4
  Rear Right: 6
  Receiver
  (SBUS)
  GND
  Power
  Power from Power Board

custom parts:
  Teensy 3.6 (Basic): The Teensy is a complete USB-based microcontoller development system, in a very small footprint, capable of implementing many types of projects. All programming is done via the USB port. No special programmer is needed, only a standard micro-USB cable and a PC or Macintosh with a USB port.
